# Fritzing sketch TheCatUnFeeder (saved by Fritzing 0.9.3b)
breadboards: 1

parts:
  Part1 = Arduino Nano (Rev3.0)
  Q1 = NPN-Transistor [package="TO92 [THT]"]
  LED1 = LED - 5mm [color="White (6500K)" package="5 mm [THT]"]
  LED2 = LED - 5mm [color="White (6500K)" package="5 mm [THT]"]
  R2 = Resistor [tolerance=±1% resistance=100 package=THT]
  R3 = Resistor [tolerance=±1% resistance=100 package=THT]
  J1 = Basic Servo
  R1 = Resistor [tolerance=±1% resistance=3.3k package=THT]
  C1 = Electrolytic Capacitor [capacitance=470µF package="100 mil [THT, electrolytic]"]
  Part2 = Adafruit TCS34725 RGB Color Sensor [part_number="Adafruit #1334"]
  J2 = Basic Servo
  PIR1 = PIR sensor
  U1 = ESP8266 WiFi Module [part_number=ESP8266]
  R4 = Resistor [tolerance=±1% resistance=1k package=THT]
  R5 = Resistor [tolerance=±1% resistance=2k package=THT]
  R6 = Resistor [tolerance=±1% resistance=10k package=THT]

nets:
  N1: Part1.D1/TX, R4.Pin_1, R5.Pin_1
  N2: Part1.D0/RX, U1.TXD
  GND: Part1.GND, Q1.E, J1.gnd, C1.-, Part2.GND, J2.gnd, PIR1.GND, R5.Pin_0
  N3: Part1.D3, J2.pulse
  N4: Part1.D4, PIR1.SIG
  N5: Part1.D6, R1.Pin_1
  N6: Part1.D7, Part2.LED_EN
  N7: Part1.D8, J1.pulse
  VIN: Part1.VIN, R2.Pin_0, R3.Pin_0, J1.vcc, C1.+, Part2.VIN, J2.vcc, PIR1.VDD
  N8: Part1.A5, Part2.SCL
  N9: Part1.A4, Part2.SDA
  N10: Q1.B, R1.Pin_0
  N11: Q1.C, LED1.cathode, LED2.cathode
  N12: LED1.anode, R3.Pin_1
  N13: LED2.anode, R2.Pin_1
  N14: U1.RXD, R4.Pin_0
  N15: U1.VCC, R6.Pin_1
  N16: U1.CH_PD, R6.Pin_0

notes:
  5v
  3.3v

custom parts:
  Adafruit TCS34725 RGB Color Sensor: Your electronics can now see in dazzling color with this lovely color light sensor. We found the best color sensor on the market, the TCS34725, which has RGB and Clear light sensing elements. An IR blocking filter, integrated on-chip and localized to the color sensing photodiodes, minimizes the IR spectral component of the incoming light and allows color measurements to be made accurately. The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
  ESP8266 WiFi Module: Generic WiFi Module based on the ESP8266 with onboard PCB antenna and UART communications

// code stored in the sketch: TheCatUnFeederV2.1.ino
/*
A Cat Un-Feeder
by Joseph Grey

Version one used RFID but that proved to be unusable because the tag had to be so 
    close to the reader
Version two uses the color temperature sensor to detect cat color.

*/

#include <Servo.h>
#include <Adafruit_TCS34725.h>

#define SS_PIN 10
#define RST_PIN 8
#define ColorLED 7   // The arduino pin that controls the onboard LED of the color temp sensor

Servo doorServo;
Adafruit_TCS34725 tcs = Adafruit_TCS34725(TCS34725_INTEGRATIONTIME_50MS, TCS34725_GAIN_4X);


int doorServoPin = 9;
int doorOpen = 90;
int doorClosed = 2;
int ledPin = 6;                // LED 
int motionPin = 4;                 // PIR Out pin 
int pirStat = 0; // PIR status

void setup() {
   pinMode(ledPin, OUTPUT);     
   pinMode(motionPin, INPUT);     
   Serial.begin(9600);
   // Color temp sensor
   tcs.begin();
   pinMode(ColorLED,OUTPUT);
   digitalWrite(ColorLED, LOW);    // Turns off the LED
  
   doorServo.attach(doorServoPin);
   doorServo.write(doorOpen);
 
}

void loop(){
 int slowDoor;
 pirStat = digitalRead(motionPin); 
 //Serial.println(pirStat);
 if (pirStat == HIGH) {            // if motion detected
   digitalWrite(ledPin, HIGH);  // turn LED ON
   digitalWrite(ColorLED, HIGH);  // turn on the LED on the color temp sensor
   uint16_t r, g, b, c, colorTemp, lux;
   getRawData_noDelay(&r, &g, &b, &c);
   colorTemp = tcs.calculateColorTemperature(r, g, b);
   Serial.println(colorTemp);
   delay(2000);
   if (colorTemp < 3000){
      for (int slowDoor = 90; slowDoor >= 2; slowDoor--)
      {
        Serial.println(slowDoor); 
        delay(10);  //Increase this time even more to slow the door down more.
        doorServo.write(slowDoor);
      }
      delay(5000);
      for (int slowDoor = 2; slowDoor <= 90; slowDoor++)
      {
        Serial.println(slowDoor); 
        delay(10);  //Increase this time even more to slow the door down more.
        doorServo.write(slowDoor);
      }
   }
  } 
 else {
   digitalWrite(ledPin, LOW); // turn LED OFF if we have no motion
   digitalWrite(ColorLED, LOW);  // turn off the LED on the color sensor
 }
}

void getRawData_noDelay(uint16_t *r, uint16_t *g, uint16_t *b, uint16_t *c)
{
  *c = tcs.read16(TCS34725_CDATAL);
  *r = tcs.read16(TCS34725_RDATAL);
  *g = tcs.read16(TCS34725_GDATAL);
  *b = tcs.read16(TCS34725_BDATAL);
}
